// Digital circuit ControlLogic.dig as structural Verilog
module ControlLogic (
  input  [2:0] OP,
  output PCsrc,
  output DataSRC,
  output OUTen,
  output WritePTR,
  output WriteData,
  output ALUsrc,
  output ALUOp
);

  wire and_5_out, and_6_out, not_1_out, not_2_out, not_3_out;

  not not_1 (not_1_out, OP[2]);
  not not_2 (not_2_out, OP[1]);
  not not_3 (not_3_out, OP[0]);
  and and_1 (PCsrc, OP[1], OP[2]);
  and and_2 (DataSRC, OP[0], not_2_out, OP[2]);
  and and_3 (OUTen, not_3_out, not_2_out, OP[2]);
  and and_4 (WritePTR, not_2_out, not_1_out);
  and and_5 (and_5_out, OP[0], not_2_out, OP[2]);
  and and_6 (and_6_out, OP[1], not_1_out);
  or or_1 (WriteData, and_5_out, and_6_out);

  assign ALUOp = OP[0];
  assign ALUsrc = OP[1];
endmodule
