// Digital circuit MainProcessor.dig as structural Verilog
module MainProcessor (
  input  [15:0] IN,
  input  clk,
  output [15:0] OUT,
  output [15:0] PC,
  output [15:0] PCOut,
  output [15:0] PTRout,
  output [15:0] MEMout
);

  wire ALUOp, ALUsrc, and_1_out, and_2_out, button_1_out, clk_t, comparator_1_eq, comparator_2_eq, DataSRC,
       dipswitch_1_out, nclk, or_1_out, OUTen, PCsrc, PCsub, WriteData, writePTR;
  wire [15:0] addsub_1_p4, addsub_2_p4, bitextender_1_p2, multiplexer_1_out, multiplexer_3_out,
       multiplexer_4_out;

  Comparator #(.Bits(3)) comparator_1 (.a(PCOut[15:13]), .b(3'b111), .eq(comparator_1_eq));  // open: gt, lt
  and and_1 (and_1_out, comparator_2_eq, PCsrc);
  and and_2 (and_2_out, comparator_1_eq, PCsrc);
  Comparator #(.Bits(16)) comparator_2 (.a(MEMout), .b({16{1'b0}}), .eq(comparator_2_eq));  // open: gt, lt
  or or_1 (or_1_out, and_1_out, and_2_out);
  Register #(.Bits(16), .isProgramCounter("true")) u_PC (.D(addsub_1_p4), .C(clk_t), .en(1'b1), .Q(PC));
  Multiplexer #(.Bits(16)) multiplexer_1 (
    .sel(or_1_out), .in_0(16'h1), .in_1(bitextender_1_p2), .out(multiplexer_1_out));
  // addsub addsub_1: pin names not known; wires that end beside it: PC, multiplexer_1_out, PCsub, addsub_1_p4
  ROM #(.AddrBits(16), .Bits(16)) ProgMem (.A(PC), .sel(1'b1), .D(PCOut));
  Button button_1 (.out(button_1_out));
  Multiplexer multiplexer_2 (.sel(dipswitch_1_out), .in_0(button_1_out), .in_1(clk), .out(clk_t));
  not not_1 (nclk, clk_t);
  DipSwitch dipswitch_1 (.out(dipswitch_1_out));
  Register #(.Bits(16)) PTR (.D(addsub_2_p4), .C(clk_t), .en(writePTR), .Q(PTRout));
  // bitExtender bitextender_1: pin names not known; wires that end beside it: PCOut[12:0], bitextender_1_p2
  Multiplexer #(.Bits(16)) multiplexer_3 (.sel(ALUsrc), .in_0(PTRout), .in_1(MEMout), .out(multiplexer_3_out));
  // addsub addsub_2: pin names not known; wires that end beside it: multiplexer_3_out, bitextender_1_p2, ALUOp, addsub_2_p4
  Multiplexer #(.Bits(16)) multiplexer_4 (.sel(DataSRC), .in_0(addsub_2_p4), .in_1(IN), .out(multiplexer_4_out));
  ControlLogic controllogic_1 (
    .OP(PCOut[15:13]), .PCsrc(PCsrc), .PCsub(PCsub), .DataSRC(DataSRC), .OUTen(OUTen), .WritePTR(writePTR),
    .WriteData(WriteData), .ALUsrc(ALUsrc), .ALUOp(ALUOp));
  RAMDualPort #(.AddrBits(16), .Bits(16)) ramdualport_1 (
    .A(PTRout), .Din(multiplexer_4_out), .str(WriteData), .C(clk_t), .ld(1'b1), .D(MEMout));
  Register #(.Bits(16)) OUTreg (.D(MEMout), .C(clk_t), .en(OUTen), .Q(OUT));
  Terminal terminal_1 (.D(MEMout), .C(clk_t), .en(OUTen));

  // Other names for the same wires on the sheet: OPcode[2:0] = PCOut[15:13]; sys_clk = clk

  // Notes on the sheet:
  //   FetchStage
  //   contents of ProgMem (hex, n*v repeats v):
  //   1,4008,c006,2001,4009,1,6001,e005,2001,8001,1,4004,c006,2001,4007
  //   ,1,6001,e005,2001,4001,8001,4007,8002,4003,8001,2,4006,c006,2001
  //   ,4007,1,6001,e005,2001,4002,8001,600c,8001,1,4006,c006,2001,4009
  //   ,1,6001,e005,2001,4001,8001,2001,8001,4003,8001,6006,8001,6008
  //   ,8001,3,4004,c006,2001,4008,1,6001,e005,2001,4001
  //   DecodeStage
  //   ExecuteStage
  //   MemoryStage
endmodule
